# Fritzing sketch Schematic (saved by Fritzing 0.4.2b)

parts:
  Arduino1 = Arduino
  J1 = Piezo Speaker
  LED2 = yellow LED - 5mm
  LED3 = Red LED - 5mm
  J2 = Infrared Proximity Sensor
  C1 = Electrolytic Capacitor [package=THT]
  R1 = Resistor [resistance=220 package=THT]
  R2 = Resistor [resistance=220 package=THT]

nets:
  GND: Arduino1.GND, J1.pin1, LED2.cathode, LED3.cathode, J2.GND, C1.+
  N1: Arduino1.D11, R1.Pin_0
  N2: Arduino1.D7, R2.Pin_0
  N3: Arduino1.D4, J1.pin2
  +5V: Arduino1.+5V, J2.Vcc, C1.-
  N4: Arduino1.A0, J2.Vout
  N5: LED2.anode, R1.Pin_1
  N6: LED3.anode, R2.Pin_1
